# Fritzing sketch mp3 (saved by Fritzing 0.9.3b)
breadboards: 1

parts:
  Часть1 = Arduino Uno (Rev3)
  DFPlayer_Mini1 = DFPlayer MINI [package="DIP (Dual Inline) [THT]"]
  SP1 = SPEAKER [package=pcb_mount_speaker]
  S1 = Momentary Switch [package=ksa_sealed_tac_switch]
  S2 = Momentary Switch [package=ksa_sealed_tac_switch]
  S3 = Momentary Switch [package=ksa_sealed_tac_switch]
  S4 = Momentary Switch [package=ksa_sealed_tac_switch]
  S5 = Momentary Switch [package=ksa_sealed_tac_switch]
  R1 = Resistor [tolerance=±5% resistance=220 package=THT]

nets:
  N1: Часть1.D10_PWM/SS, R1.Pin_1
  N2: Часть1.D11_PWM/MOSI, DFPlayer_Mini1.TX
  N3: Часть1.D2, S1.2
  N4: Часть1.D3_PWM, S2.2
  N5: Часть1.D4, S3.2
  N6: Часть1.D5_PWM, S4.2
  N7: Часть1.D6_PWM, S5.2
  5V: Часть1.5V, DFPlayer_Mini1.VCC
  N8: Часть1.GND, DFPlayer_Mini1.GND#6, S1.3, S2.3, S3.3, S4.3, S5.3
  N9: DFPlayer_Mini1.RX, R1.Pin_0
  N10: DFPlayer_Mini1.SPK1, SP1.-
  N11: DFPlayer_Mini1.SPK2, SP1.+

custom parts:
  DFPlayer MINI: MP3 module by DFRobot.com for playing Music from an SD-Card. Supports WAV and MP3 files.
